# Fritzing sketch b3 (saved by Fritzing 0.9.5d)
breadboards: 1

parts:
  M1 = DOIT Esp32 DevKit v1 (30 pins long, 11 pins width) [part_number=ESP32S-PIN30]
  LED1 = LED - 5mm [color="Red (633nm)" package="5 mm [THT]"]
  U1 = POT [package=pot_alpha_rv16af-20]

nets:
  N1: M1.3V3, U1.A
  N2: M1.GND, LED1.cathode, U1.E
  N3: M1.D4, M1.RX2, M1.TX2, M1.D5, M1.D18
  N4: M1.RX0, M1.TX0, M1.D22, M1.D23
  N5: M1.EN, M1.VP, M1.VN, M1.D34
  N6: M1.D33, M1.D25, M1.D26, M1.D27, M1.D14

custom parts:
  DOIT Esp32 DevKit v1 (30 pins long, 11 pins width): The DOIT Esp32 DevKit v1 is one of the development board created by DOIT to evaluate the ESP-WROOM-32 module. It is based on the ESP32 microcontroller that boasts Wifi, Bluetooth, Ethernet and Low Power support all in a single chip. (vanepp) made breadboard work, adjusted pin numbering and labels and reduced size of schematic and cleaned up pcb. This chip is 30pins long (2 x15) and 11 pins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
